# Fritzing sketch 40-zif (saved by Fritzing 1.0.6)

parts:
  Компонент1 = Arduino Mega 2560 (Rev3)
  U1 = ZIFSOCKET-40-6 [package=dil40-6-zif_socket]
  J1 = female pin header, 1 pin [form="♀ (female)"]
  J2 = female pin header, 1 pin [form="♀ (female)"]
  J3 = male pin header, 20 pins [form="♂ (male)"]  # not connected
  J4 = male pin header, 20 pins [form="♂ (male)"]  # not connected

nets:
  N1: Компонент1.A8, U1.P$20
  N2: Компонент1.A9, U1.P$21
  N3: Компонент1.A10, U1.P$19
  N4: Компонент1.A11, U1.P$22
  N5: Компонент1.A12, U1.P$18
  N6: Компонент1.A13, U1.P$23
  N7: Компонент1.A14, U1.P$17
  N8: Компонент1.A15, U1.P$24
  N9: Компонент1.D21/SCL, U1.P$38
  N10: Компонент1.D20/SDA, U1.P$3
  N11: Компонент1.D19/RX1, U1.P$39
  N12: Компонент1.D18/TX1, U1.P$2
  N13: Компонент1.D17_PWM/RX2, U1.P$40
  N14: Компонент1.D16_PWM/TX2, U1.P$1
  N15: Компонент1.5V, J2.pin1
  N16: Компонент1.D22, U1.P$4
  N17: Компонент1.D23, U1.P$37
  N18: Компонент1.D24, U1.P$5
  N19: Компонент1.D25, U1.P$36
  N20: Компонент1.D26, U1.P$6
  N21: Компонент1.D27, U1.P$35
  N22: Компонент1.D28, U1.P$7
  N23: Компонент1.D29, U1.P$34
  N24: Компонент1.D30, U1.P$8
  N25: Компонент1.D31, U1.P$33
  N26: Компонент1.D32, U1.P$9
  N27: Компонент1.D33, U1.P$32
  N28: Компонент1.D34, U1.P$10
  N29: Компонент1.D35, U1.P$31
  N30: Компонент1.D42, U1.P$11
  N31: Компонент1.D43, U1.P$30
  N32: Компонент1.D44, U1.P$12
  N33: Компонент1.D45, U1.P$29
  N34: Компонент1.D46, U1.P$13
  N35: Компонент1.D47, U1.P$28
  N36: Компонент1.D48, U1.P$14
  N37: Компонент1.D49, U1.P$27
  N38: Компонент1.D50, U1.P$15
  N39: Компонент1.D51, U1.P$26
  N40: Компонент1.D52, U1.P$16
  N41: Компонент1.D53, U1.P$25
  N42: Компонент1.GND, J1.pin1
